// Logisim project four-bit-ALU.circ as structural Verilog: 1 circuit, main circuit main
module main (
  input  AInvert,
  input  BInvert,
  input  [1:0] Operation,
  input  in_4
);

  wire and_1_out, and_2_out, and_3_out, and_4_out, and_5_out, and_6_out, and_7_out, and_8_out, and_9_out,
       and_10_out, and_11_out, and_12_out, and_13_out, and_14_out, and_15_out, and_16_out, and_17_out,
       and_18_out, and_19_out, and_20_out, and_21_out, and_22_out, and_23_out, and_24_out, and_25_out,
       and_26_out, and_27_out, and_28_out, and_29_out, and_30_out, and_31_out, and_32_out, and_33_out,
       and_34_out, clock_1_out, multiplexer_1_out, multiplexer_2_out, multiplexer_3_out, multiplexer_4_out,
       multiplexer_5_out, multiplexer_6_out, multiplexer_7_out, multiplexer_8_out, not_1_out, not_2_out,
       not_3_out, not_4_out, not_5_out, not_6_out, not_7_out, not_8_out, not_9_out, not_10_out, not_11_out,
       not_12_out, not_13_out, not_14_out, not_15_out, not_16_out, not_17_out, not_18_out, not_19_out,
       not_20_out, not_21_out, not_22_out, not_23_out, not_24_out, not_25_out, not_26_out, not_27_out,
       not_28_out, not_29_out, not_30_out, not_31_out, not_32_out, not_33_out, or_1_out, or_2_out, or_3_out,
       or_4_out, or_5_out, or_6_out, or_7_out, or_8_out, or_9_out, or_10_out, or_11_out, or_12_out,
       or_13_out, or_14_out;
  wire [3:0] multiplexer_9_out, random_1_out, random_2_out;

  Clock clock_1 (.out(clock_1_out));
  Random #(.width(4)) random_1 (.clk(clock_1_out), .out(random_1_out));  // open: next, clr
  Random #(.width(4)) random_2 (.clk(clock_1_out), .out(random_2_out));  // open: next, clr
  Multiplexer multiplexer_1 (
    .in0(random_1_out[0]), .in1(not_1_out), .out(multiplexer_1_out), .sel(AInvert));  // open: en
  not not_1 (not_1_out, random_1_out[0]);
  not not_2 (not_2_out, random_2_out[0]);
  Multiplexer multiplexer_2 (
    .in0(random_1_out[1]), .in1(not_3_out), .out(multiplexer_2_out), .sel(AInvert));  // open: en
  not not_3 (not_3_out, random_1_out[1]);
  not not_4 (not_4_out, random_2_out[1]);
  not not_5 (not_5_out, random_1_out[2]);
  Multiplexer multiplexer_3 (
    .in0(random_1_out[3]), .in1(not_6_out), .out(multiplexer_3_out), .sel(AInvert));  // open: en
  not not_6 (not_6_out, random_1_out[3]);
  not not_7 (not_7_out, random_2_out[3]);
  Multiplexer multiplexer_4 (
    .in0(random_2_out[0]), .in1(not_2_out), .out(multiplexer_4_out), .sel(BInvert));  // open: en
  Multiplexer multiplexer_5 (
    .in0(random_2_out[1]), .in1(not_4_out), .out(multiplexer_5_out), .sel(BInvert));  // open: en
  Multiplexer multiplexer_6 (
    .in0(random_1_out[2]), .in1(not_5_out), .out(multiplexer_6_out), .sel(AInvert));  // open: en
  Multiplexer multiplexer_7 (
    .in0(random_2_out[2]), .in1(not_8_out), .out(multiplexer_7_out), .sel(BInvert));  // open: en
  not not_8 (not_8_out, random_2_out[2]);
  Multiplexer multiplexer_8 (
    .in0(random_2_out[3]), .in1(not_7_out), .out(multiplexer_8_out), .sel(BInvert));  // open: en
  not not_9 (not_9_out, multiplexer_4_out);
  not not_10 (not_10_out, multiplexer_5_out);
  not not_11 (not_11_out, multiplexer_7_out);
  not not_12 (not_12_out, multiplexer_8_out);
  and and_1 (and_1_out, multiplexer_1_out, multiplexer_4_out);
  or or_1 (or_1_out, multiplexer_4_out, multiplexer_1_out);
  not not_13 (not_13_out, multiplexer_1_out);
  not not_14 (not_14_out, multiplexer_1_out);
  not not_15 (not_15_out, BInvert);
  not not_16 (not_16_out, multiplexer_4_out);
  not not_17 (not_17_out, BInvert);
  and and_2 (and_2_out, multiplexer_2_out, multiplexer_5_out);
  or or_2 (or_2_out, multiplexer_5_out, multiplexer_2_out);
  not not_18 (not_18_out, multiplexer_2_out);
  not not_19 (not_19_out, multiplexer_2_out);
  not not_20 (not_20_out, or_6_out);
  not not_21 (not_21_out, multiplexer_5_out);
  not not_22 (not_22_out, or_6_out);
  and and_3 (and_3_out, multiplexer_6_out, multiplexer_7_out);
  or or_3 (or_3_out, multiplexer_7_out, multiplexer_6_out);
  not not_23 (not_23_out, multiplexer_6_out);
  not not_24 (not_24_out, multiplexer_6_out);
  not not_25 (not_25_out, or_8_out);
  not not_26 (not_26_out, multiplexer_7_out);
  not not_27 (not_27_out, or_8_out);
  and and_4 (and_4_out, multiplexer_3_out, multiplexer_8_out);
  or or_4 (or_4_out, multiplexer_8_out, multiplexer_3_out);
  not not_28 (not_28_out, multiplexer_3_out);
  not not_29 (not_29_out, multiplexer_3_out);
  not not_30 (not_30_out, or_10_out);
  not not_31 (not_31_out, multiplexer_8_out);
  not not_32 (not_32_out, or_10_out);
  and and_5 (and_5_out, not_13_out, not_9_out, BInvert);
  and and_6 (and_6_out, not_14_out, multiplexer_4_out, not_15_out);
  and and_7 (and_7_out, multiplexer_1_out, not_16_out, not_17_out);
  and and_8 (and_8_out, multiplexer_1_out, multiplexer_4_out, BInvert);
  and and_9 (and_9_out, multiplexer_4_out, BInvert);
  and and_10 (and_10_out, multiplexer_1_out, BInvert);
  and and_11 (and_11_out, multiplexer_1_out, multiplexer_4_out);
  and and_12 (and_12_out, not_18_out, not_10_out, or_6_out);
  and and_13 (and_13_out, not_19_out, multiplexer_5_out, not_20_out);
  and and_14 (and_14_out, multiplexer_2_out, not_21_out, not_22_out);
  and and_15 (and_15_out, multiplexer_2_out, multiplexer_5_out, or_6_out);
  and and_16 (and_16_out, multiplexer_5_out, or_6_out);
  and and_17 (and_17_out, multiplexer_2_out, or_6_out);
  and and_18 (and_18_out, multiplexer_2_out, multiplexer_5_out);
  and and_19 (and_19_out, not_23_out, not_11_out, or_8_out);
  and and_20 (and_20_out, not_24_out, multiplexer_7_out, not_25_out);
  and and_21 (and_21_out, multiplexer_6_out, not_26_out, not_27_out);
  and and_22 (and_22_out, multiplexer_6_out, multiplexer_7_out, or_8_out);
  and and_23 (and_23_out, multiplexer_7_out, or_8_out);
  and and_24 (and_24_out, multiplexer_6_out, or_8_out);
  and and_25 (and_25_out, multiplexer_6_out, multiplexer_7_out);
  and and_26 (and_26_out, not_28_out, not_12_out, or_10_out);
  and and_27 (and_27_out, not_29_out, multiplexer_8_out, not_30_out);
  and and_28 (and_28_out, multiplexer_3_out, not_31_out, not_32_out);
  and and_29 (and_29_out, multiplexer_3_out, multiplexer_8_out, or_10_out);
  and and_30 (and_30_out, multiplexer_8_out, or_10_out);
  and and_31 (and_31_out, multiplexer_3_out, or_10_out);
  and and_32 (and_32_out, multiplexer_3_out, multiplexer_8_out);
  Multiplexer #(.select(2)) multiplexer_9 (
    .in0(and_1_out), .in1(or_1_out), .in2(or_5_out), .in3(or_11_out), .out(multiplexer_9_out[0]),
    .sel(Operation));  // open: en
  Multiplexer #(.select(2)) multiplexer_10 (
    .in0(and_2_out), .in1(or_2_out), .in2(or_7_out), .in3(1'b0), .out(multiplexer_9_out[1]), .sel(Operation));  // open: en
  Multiplexer #(.select(2)) multiplexer_11 (
    .in0(and_3_out), .in1(or_3_out), .in2(or_9_out), .in3(1'b0), .out(multiplexer_9_out[2]), .sel(Operation));  // open: en
  Multiplexer #(.select(2)) multiplexer_12 (
    .in0(and_4_out), .in1(or_4_out), .in2(or_11_out), .in3(1'b0), .out(multiplexer_9_out[3]), .sel(Operation));  // open: en
  or or_5 (or_5_out, and_5_out, and_6_out, and_7_out, and_8_out);
  or or_6 (or_6_out, and_9_out, and_10_out, and_11_out);
  or or_7 (or_7_out, and_12_out, and_13_out, and_14_out, and_15_out);
  or or_8 (or_8_out, and_16_out, and_17_out, and_18_out);
  or or_9 (or_9_out, and_19_out, and_20_out, and_21_out, and_22_out);
  or or_10 (or_10_out, and_23_out, and_24_out, and_25_out);
  or or_11 (or_11_out, and_26_out, and_27_out, and_28_out, and_29_out);
  or or_12 (or_12_out, and_30_out, and_31_out, and_32_out);
  TTY #(.trigger("falling")) tty_1 (.data({3'b011, multiplexer_9_out}), .clk(clock_1_out), .clr(in_4));  // open: we
  or or_13 (or_13_out, or_12_out, or_10_out);
  and and_33 (and_33_out, or_12_out, or_10_out);
  or or_14 (or_14_out, or_5_out, or_7_out, or_9_out, or_11_out);
  and and_34 (and_34_out, or_13_out, ~and_33_out);  // AND_Gate
  not not_33 (not_33_out, or_14_out);
  LED Overflow (.in(and_34_out));
  LED Equals (.in(not_33_out));
endmodule
